# Fritzing sketch ExternalLED (saved by Fritzing 0.9.9b)
breadboards: 1

parts:
  Part1 = Arduino Uno (Rev3)
  LED1 = smd LED [color="Red (635nm)" package="1206 [SMD]"]
  LED2 = smd LED [color="Yellow (592nm)" package="1206 [SMD]"]
  LED3 = smd LED [color="Green (555nm)" package="1206 [SMD]"]
  R1 = Resistor [tolerance=±5% resistance=220 package="0805 [SMD]"]
  R2 = Resistor [tolerance=±5% resistance=220 package="0805 [SMD]"]
  R3 = Resistor [tolerance=±5% resistance=220 package="0805 [SMD]"]

nets:
  N1: Part1.D8, LED3.anode
  N2: Part1.D9_PWM, LED1.anode
  N3: Part1.GND, R1.Pin_0, R2.Pin_0, R3.Pin_0
  N4: Part1.D7, LED2.anode
  N5: LED1.cathode, R1.Pin_1
  N6: LED2.cathode, R2.Pin_1
  N7: LED3.cathode, R3.Pin_1
