# Fritzing sketch MicroServo (saved by Fritzing 0.9.9b)

parts:
  Part1 = Arduino Uno (Rev3) - ICSP
  J1 = Basic Servo

nets:
  N1: Part1.D11_PWM/MOSI, J1.pulse
  5V: Part1.5V, J1.vcc
  GND: Part1.GND, J1.gnd
