# Fritzing sketch ADC (saved by Fritzing 0.9.9b)
breadboards: 1

parts:
  Part1 = Arduino Uno (Rev3)
  R1 = Resistor [tolerance=±5% resistance=10k package="2010 [SMD]"]
  C1 = Tantalum Capacitor [capacitance=10nF voltage=35V package="C 6032 [SMD, tantalum]"]

nets:
  N1: Part1.A0, R1.Pin_0, C1.+
  N2: Part1.GND, C1.-
  N3: Part1.D6_PWM, R1.Pin_1
